// Digital circuit CORE.dig as structural Verilog
module CORE (
  input  clk,
  input  RST,
  input  CLR
);

  wire ALUD_CO, ALUDH_OE, ALUDL_OE, ALUS_OE, and_3_out, and_4_out, BR_Q, button_1_out, CLK_t,
       comparator_1_eq, comparator_1_gt, comparator_1_lt, DC_JUMP, IMMED_OE, IRQ_OE, not_1_out, not_2_out,
       RAM_OE, RAM_WE, RF_HWE, RF_LWE, RF_SFR, RFSRCR_WE, ROM_OE, SFR_OE, SR_WE, WR_WE, XRAM_OE;
  wire [2:0] BR_SRC, BUS_SRC, JUMP_TYPE;
  wire [3:0] ALUSD_FUNC, RF_SRC;
  wire [5:0] multiplexer_2_out;
  wire [6:0] and_2_out;
  wire [7:0] DBUS, IMMED, RF_Q, SR_q, WR_q;
  wire [7:4] RFSRCR_q;
  wire [11:0] ADDRESS, dcouter_1_q;
  wire [47:44] DECODER_2_d;

  Comparator #(.Bits(8)) comparator_1 (
    .a(RF_Q), .b(IMMED), .gt(comparator_1_gt), .eq(comparator_1_eq), .lt(comparator_1_lt));
  Decoder #(.Selector_Bits(3)) decoder_1 (
    .sel(BUS_SRC), .out_0(ALUS_OE), .out_1(ALUDL_OE), .out_2(ALUDH_OE), .out_3(IMMED_OE), .out_4(RAM_OE),
    .out_5(XRAM_OE), .out_6(ROM_OE), .out_7(IRQ_OE));
  DCOUTER dcouter_1 (.CLK(CLK_t), .CLR(CLR), .CNT(1'b1), .LE(DC_JUMP), .D(ADDRESS), .Q(dcouter_1_q));
  Multiplexer #(.Selector_Bits(3)) multiplexer_1 (
    .sel(JUMP_TYPE), .in_0(1'b0), .in_1(1'b1), .in_2(comparator_1_gt), .in_3(comparator_1_eq),
    .in_4(comparator_1_lt), .in_5(BR_Q), .in_6(RST), .in_7(1'b0), .out(DC_JUMP));
  // Probe on dcouter_1_q
  ROM #(.AddrBits(12), .Bits(48)) DECODER_2 (
    .A(dcouter_1_q), .sel(1'b1),
    .D({DECODER_2_d, IMMED, ADDRESS, JUMP_TYPE, ALUSD_FUNC, RAM_WE, RFSRCR_WE, BR_SRC, SR_WE, WR_WE, BUS_SRC, RF_SFR, RF_HWE, RF_LWE, RF_SRC}));
  Register #(.Bits(8)) RFSRCR (.D(DBUS), .C(CLK_t), .en(RFSRCR_WE), .Q({RFSRCR_q, and_2_out[3:0]}));
  and and_1 (and_2_out[5], RFSRCR_q[4], RAM_WE);
  and and_2 (and_2_out[6], RFSRCR_q[4], RAM_OE);
  Multiplexer #(.Bits(7)) multiplexer_2 (
    .sel(RF_SFR), .in_0({1'b0, RF_HWE, RF_LWE, RF_SRC}),
    .in_1({and_2_out[6:5], and_2_out[5], and_2_out[3:0]}), .out({SFR_OE, multiplexer_2_out}));
  // Probe on RF_SRC
  // Probe on RF_LWE
  // Probe on RF_HWE
  // Probe on RF_SFR
  // Probe on BUS_SRC
  // Probe on WR_WE
  // Probe on SR_WE
  // Probe on BR_SRC
  // Probe on RFSRCR_WE
  // Probe on RAM_WE
  // Probe on ALUSD_FUNC
  // Probe on JUMP_TYPE
  // Probe on ADDRESS
  // Probe on IMMED
  Button button_1 (.out(button_1_out));
  // reg_file RF: pin names not known; wires that end beside it: CLK_t, multiplexer_2_out[3:0], DBUS, multiplexer_2_out[4], multiplexer_2_out[5], RF_Q
  BR BR (.CLK(CLK_t), .CLR(CLR), .S(BR_SRC), .ALUDF(ALUD_CO), .ALUSF(ALUD_CO), .A0(RF_Q[0]), .A7(RF_Q[7]), .Q(BR_Q));
  // SwitchDT switchdt_1: pin names not known; wires that end beside it: clk, button_1_out, CLK_t
  // Probe on DBUS
  PullDown #(.Bits(8)) pulldown_1 (.out(DBUS));
  // Probe on RF_Q
  reg8clr WR (.D(DBUS), .CLK(CLK_t), .CLR(CLR), .LE(WR_WE), .Q(WR_q));
  reg8clr SR (.D(DBUS), .CLK(CLK_t), .CLR(CLR), .LE(SR_WE), .Q(SR_q));
  not not_1 (not_1_out, CLK_t);
  // Probe on WR_q
  // Probe on SR_q
  and and_3 (and_3_out, CLK_t, not_1_out);
  and and_4 (and_4_out, RAM_WE, and_3_out);
  // Probe CLKSP on and_3_out
  // Probe on {SR_q, WR_q}
  not not_2 (not_2_out, SR_q[7]);
  assign DBUS = IMMED_OE ? IMMED : 8'bz;  // Driver driver_1
  ALU ALU (
    .A(RF_Q), .B(WR_q), .S(ALUSD_FUNC), .CI(BR_Q), .nSOE(ALUS_OE), .nDLOE(ALUDL_OE), .nDHOE(ALUDH_OE),
    .O(DBUS), .CO(ALUD_CO));
  ROM #(.AddrBits(16), .Bits(8)) ROM (.A({SR_q, WR_q}), .sel(ROM_OE), .D(DBUS));
  RAMSinglePortSel #(.AddrBits(7), .Bits(8)) RAM (.A(SR_q[6:0]), .CS(not_2_out), .WE(and_4_out), .OE(RAM_OE), .D(DBUS));
  assign DBUS = SFR_OE ? RF_Q : 8'bz;  // Driver driver_2

  // Notes on the sheet:
  //   clk: Hz: 360
  //   contents of DECODER_2 (hex, n*v repeats v):
  //   12ac80488,80889,33a,580,85100,c3133,450b8,400b9,8007f80000a,c004580000a,e002680000a,
  //   f001780000a,f801180040a,a00bc,80403,1a080c,230,f401480000a,f601380000a,f501480000a,
  //   f201680000a,f301680000a,f101780000a,e801f80000a,ec01c80000a,ee01b80000a,ef01b80000a,
  //   ed01c80000a,ea01e80000a,eb01e80000a,e901f80000a,e402380000a,e602280000a,e702280000a,
  //   e502380000a,e202580000a,e302580000a,e102680000a,d003680000a,d802f80000a,dc02c80000a,
  //   de02b80000a,df02b80000a,dd02c80000a,da02e80000a,db02e80000a,d902f80000a,d403380000a,
  //   d603280000a,d703280000a,d503380000a,d203580000a,d303580000a,d103680000a,c803e80000a,
  //   cc03b80000a,ce03a80000a,cf03a80000a,cd03b80000a,ca03d80000a,cb03d80000a,c903e80000a,
  //   c404280000a,c604180000a,c704180000a,c504280000a,c204480000a,c304480000a,c104580000a,
  //   a006880000a,b005680000a,b804f80000a,bc04c80000a,be04b80000a,bf04b80000a,bd04c80000a,
  //   ba04e80000a,bb04e80000a,b904f80000a,b405380000a,b605280000a,b705280000a,b505380000a,
  //   b205580000a,b305580000a,b105680000a,a805e80000a,ac05b80000a,ae05a80000a,af05a80000a,
  //   ad05b80000a,aa05d80000a,ab05d80000a,a905e80000a,a406280000a,a606180000a,a706180000a,
  //   a506280000a,a206780000a,a306780000a,3580,45034,112240035,a106880000a,9007080000a,
  //   9806a80000a,9406d80000a,9606c80000a,9506d80000a,9206f80000a,9306f80000a,9107080000a,
  //   8807880000a,8c07580000a,8e07480000a,8f07480000a,8d07580000a,8a07780000a,8b07780000a,
  //   8907880000a,8407c80000a,8607b80000a,8707b80000a,8507c80000a,8207e80000a,8307e80000a,
  //   8107f80000a,400d080000a,600b180000a,700a280000a,7808a80000a,7c08780000a,7e08680000a,
  //   7f08680000a,7d08780000a,7a08980000a,7b08980000a,7908a80000a,7409f80000a,7608d80000a,
  //   7708d80000a,7509980000a,80488,80889,b3c,3580,45438,40839,6800c,10340,3580,45038,112240039,
  //   80488,80889,330,3580,450b8,1122400b9,720a180000a,730a180000a,710a280000a,680aa80000a,
  //   6c0a780000a,6e0a680000a,6f0a680000a,6d0a780000a,6a0a980000a,6b0a980000a,690aa80000a,
  //   640ae80000a,660ad80000a,670ad80000a,650ae80000a,620b080000a,630b080000a,610b180000a,
  //   500c180000a,580ba80000a,5c0b780000a,5e0b680000a,5f0b680000a,5d0b780000a,5a0b980000a,
  //   5b0b980000a,590ba80000a,540be80000a,560bd80000a,570bd80000a,550be80000a,520c080000a,
  //   530c080000a,510c180000a,480c980000a,4c0c680000a,4e0c580000a,4f0c580000a,4d0c680000a,
  //   4a0c880000a,4b0c880000a,490c980000a,440cd80000a,460cc80000a,470cc80000a,450cd80000a,
  //   420cf80000a,430cf80000a,410d080000a,200f080000a,300e180000a,380da80000a,3c0d780000a,
  //   3e0d680000a,3f0d680000a,3d0d780000a,3a0d980000a,3b0d980000a,390da80000a,340de80000a,
  //   360dd80000a,370dd80000a,350de80000a,320e080000a,330e080000a,310e180000a,280e980000a,
  //   2c0e680000a,2e0e580000a,2f0e580000a,2d0e680000a,2a0e880000a,2b0e880000a,290e980000a,
  //   240ed80000a,260ec80000a,270ec80000a,250ed80000a,220ef80000a,230ef80000a,210f080000a,
  //   1010080000a,180f980000a,1c0f680000a,1e0f580000a,1f0f580000a,1d0f680000a,1a0f880000a,
  //   1b0f880000a,190f980000a,140fd80000a,160fc80000a,170fc80000a,150fd80000a,120ff80000a,
  //   130ff80000a,1110080000a,810880000a,c10580000a,e10480000a,f10480000a,d10580000a,a10780000a,
  //   b10780000a,910880000a,410d80000a,610b80000a,710b80000a,510c80000a,100030,211080000a,
  //   311080000a,80030,111280000a,112200000,80000880486,3bc,e04bc,100080000c,80487,1600bc,
  //   8048b,a00bd,a00be,80487,16348d,6500c,a00000,10048c,e00be,40000e,c00bb,100832,90088,
  //   100832,90089,2043c,1b9,2a00b8,1b0,1b1,1b2,1b3,1b4,1b5,1b6,1b7,1b8,1b9,1ba,12ac001bb,
  //   200000
  //   contents of ROM (hex, n*v repeats v):
  //   75,7f,66,75,1,1,75,2,2,75,3,3,75,4,4,75,5,5,75,6,6,75,7,7,75,8,8,75,9,9,75,a,a,75,
  //   b,b,75,c,c,75,d,d,75,e,e,75,f,f,75,10,10,75,11,11,75,12,12,75,13,13,75,14,14,75,15,
  //   15,75,16,16,75,17,17,75,18,18,75,19,19,75,1a,1a,75,1b,1b,75,1c,1c,75,1d,1d,75,1e,
  //   1e,75,1f,1f,75,20,20,75,21,21,75,22,22,75,23,23,75,24,24,75,25,25,75,26,26,75,27,
  //   27,75,28,28,75,29,29,75,2a,2a,75,2b,2b,75,2c,2c,75,2d,2d,75,2e,2e,75,2f,2f,75,30,
  //   30,75,31,31,75,32,32,75,33,33,75,34,34,75,35,35,75,36,36,75,37,37,75,38,38,75,39,
  //   39,75,3a,3a,75,3b,3b,75,3c,3c,75,3d,3d,75,3e,3e,75,3f,3f,75,40,40,75,41,41,75,42,
  //   42,75,43,43,75,44,44,75,45,45,75,46,46,75,47,47,75,48,48,75,49,49,75,4a,4a,75,4b,
  //   4b,75,4c,4c,75,4d,4d,75,4e,4e,75,4f,4f,75,50,50,75,51,51,75,52,52,75,53,53,75,54,
  //   54,75,55,55,75,56,56,75,57,57,75,58,58,75,59,59,75,5a,5a,75,5b,5b,75,5c,5c,75,5d,
  //   5d,75,5e,5e,75,5f,5f,75,60,60,75,61,61,75,62,62,75,63,63,75,64,64,75,65,65,75,66,
  //   66,75,67,67,75,68,68,75,69,69,75,6a,6a,75,6b,6b,75,6c,6c,75,6d,6d,75,6e,6e,75,6f,
  //   6f,75,70,70,75,71,71,75,72,72,75,73,73,75,74,74,75,75,75,75,76,76,75,77,77,75,78,
  //   78,75,79,79,75,7a,7a,75,7b,7b,75,7c,7c,75,7d,7d,75,7e,7e,75,7f,7f,75,80,80,75,81,
  //   81,75,82,82,75,83,83,75,84,84,75,85,85,75,86,86,75,87,87,75,88,88,75,89,89,75,8a,
  //   8a,75,8b,8b,75,8c,8c,75,8d,8d,75,8e,8e,75,8f,8f,75,90,90,75,91,91,75,92,92,75,93,
  //   93,75,94,94,75,95,95,75,96,96,75,97,97,75,98,98,75,99,99,75,9a,9a,75,9b,9b,75,9c,
  //   9c,75,9d,9d,75,9e,9e,75,9f,9f,75,a0,a0,75,a1,a1,75,a2,a2,75,a3,a3,75,a4,a4,75,a5,
  //   a5,75,a6,a6,75,a7,a7,75,a8,a8,75,a9,a9,75,aa,aa,75,ab,ab,75,ac,ac,75,ad,ad,75,ae,
  //   ae,75,af,af,75,b0,b0,75,b1,b1,75,b2,b2,75,b3,b3,75,b4,b4,75,b5,b5,75,b6,b6,75,b7,
  //   b7,75,b8,b8,75,b9,b9,75,ba,ba,75,bb,bb,75,bc,bc,75,bd,bd,75,be,be,75,bf,bf,75,c0,
  //   c0,75,c1,c1,75,c2,c2,75,c3,c3,75,c4,c4,75,c5,c5,75,c6,c6,75,c7,c7,75,c8,c8,75,c9,
  //   c9,75,ca,ca,75,cb,cb,75,cc,cc,75,cd,cd,75,ce,ce,75,cf,cf,75,d0,d0,75,d1,d1,75,d2,
  //   d2,75,d3,d3,75,d4,d4,75,d5,d5,75,d6,d6,75,d7,d7,75,d8,d8,75,d9,d9,75,da,da,75,db,
  //   db,75,dc,dc,75,dd,dd,75,de,de,75,df,df,75,e0,e0,75,e1,e1,75,e2,e2,75,e3,e3,75,e4,
  //   e4,75,e5,e5,75,e6,e6,75,e7,e7,75,e8,e8,75,e9,e9,75,ea,ea,75,eb,eb,75,ec,ec,75,ed,
  //   ed,75,ee,ee,75,ef,ef,75,f0,f0,75,f1,f1,75,f2,f2,75,f3,f3,75,f4,f4,75,f5,f5,75,f6,
  //   f6,75,f7,f7,75,f8,f8,75,f9,f9,75,fa,fa,75,fb,fb,75,fc,fc,75,fd,fd,75,fe,fe,75,ff,
  //   ff
endmodule
